# Fritzing sketch sketch (saved by Fritzing 0.9.10b)
breadboards: 2

parts:
  Composant1 = Adafruit HUZZAH32 ESP32 Feather [part_number="Adafruit #3405"]
  LED1 = LED - 3mm [color="Red (633nm)" current=0.030 package="3 mm [THT]"]
  S1 = Pushbutton [package="[THT]"]
  Composant2 = Adafruit APDS-9960 [part_number="Adafruit #3595"]  # not connected
  R1 = Resistor [tolerance=±5% resistance=330k package="0603 [SMD]"]
  U1 = LIPO-110mAh [package=lipo-110]  # not connected

nets:
  N1: Composant1.GND, LED1.cathode, S1.Pin_3, S1.Pin_4
  N2: Composant1.IO27_A10, R1.Pin_1
  N3: Composant1.IO14_A6, S1.Pin_1, S1.Pin_2
  N4: LED1.anode, R1.Pin_0

custom parts:
  Adafruit APDS-9960: The APDS9960 from Avago Technologies has an integrated IR LED and driver, along with four directional photodiodes that sense reflected IR energy from the LED. It's proximity detection feature allows it to measure the distance an object is from the front of the sensor (up to a few centimeters) with 8 bit resolution. Since there are four IR sensors, you can measure the changes in light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
